# Fritzing sketch wiring_schematic (saved by Fritzing 0.9.9b)
breadboards: 1

parts:
  Mod1 = Raspberry Pi 4B
  R1 = Resistor [tolerance=±5% resistance=330 package="0402 [SMD]"]
  LED1 = LED - 5mm [color="Red (633nm)" current=0.030 package="5 mm [THT]"]
  A1 = DHT22 module

nets:
  N1: Mod1.5V, R1.Pin_0, A1.+
  N2: Mod1.GPIO2, A1.Out
  N3: Mod1.GND, A1.-
  N4: Mod1.GPIO21, LED1.cathode
  N5: R1.Pin_1, LED1.anode

custom parts:
  DHT22 module: DHT22 module. Pins VCC Data GND.
